# Fritzing sketch schematics (saved by Fritzing 1.0.3b)

parts:
  Componente1 = Arduino Nano (Rev3.0)
  M1 = ph-4502c_1

nets:
  N1: Componente1.GND, M1.connector3, M1.connector4
  N2: Componente1.VIN, M1.connector5
  N3: Componente1.A1, M1.connector0
  N4: Componente1.A0, M1.connector2

notes:
  I2C data
  I2C clock
